# Fritzing sketch BreakInMotor (saved by Fritzing 0.9.3b)
breadboards: 1

parts:
  U1 = TA7291P [package=HSIP10-P-2.54(THT)]
  VCC2 = Battery
  パーツ1 = Arduino Pro Mini (5V)
  VCC1 = Battery
  VCC3 = Battery
  M1 = DC Motor

nets:
  GND: U1.GND, VCC2.-, パーツ1.GND, VCC3.-
  N1: U1.OUT1, M1.pin_2
  N2: U1.IN1, パーツ1.D8
  N3: U1.IN2, パーツ1.D9
  VCC: U1.Vcc, パーツ1.VCC, VCC1.+
  N4: U1.Vs, VCC3.+
  N5: U1.OUT2, M1.pin_1
  N6: VCC2.+, VCC1.-

custom parts:
  TA7291P: The IC are Full-Bridge Driver. 4 modes available (CW / CCW / STOP / BRAKE) and PWM control. Output current:1.0 A (AVE.) 2.0 A (PEAK)
